# Fritzing sketch ProjetoEstacaoMetereologica (1) (1) (saved by Fritzing 0.9.3b)
circuit board: 8.65945cm x 6.28218cm
breadboards: 1

parts:
  Componente1 = Arduino Uno (Rev3)
  DHT1 = DHT22 Humidity and Temperature Sensor
  Componente2 = Adafruit BMP180
  R2 = Resistor [tolerance=±5% resistance=4.7k package=THT]
  R1 = Resistor [tolerance=±5% resistance=1.5k package=THT]
  Componente4 = Real Time Clock Module - DS1307 RTC Breakout Board
  Componente5 = LCD1602-I2C
  J1 = female pin header, 4 pins [form="♀ (female)"]

nets (from the pcb view):
  N1: Componente1.A0, Componente2.SDA, Componente5.SDA
  N2: Componente1.A1, Componente2.SCL, Componente5.SCL
  N3: Componente1.A4/SDA, Componente4.SDA
  N4: Componente1.A5/SCL, DHT1.DATA, Componente4.SCL
  GND: Componente1.GND, DHT1.GND, Componente2.GND, R2.Pin_0, Componente4.GND, Componente5.GND, J1.pin3
  N5: Componente1.D0/RX, J1.pin2
  N6: Componente1.D1/TX, R1.Pin_0
  3V3: Componente1.3V3, Componente2.+3V3
  5V: Componente1.5V, DHT1.VDD, Componente4.5V, Componente5.VCC, J1.pin4
  N7: R2.Pin_1, R1.Pin_1, J1.pin1

notes:
  Estação Meteorologica.
  sensores utilizados:
  Modulo de relógio DS1307;
  Modulo de pressão BMP180;
  Sensor de humidade e temperatura DHT22;
  Outros:
  Modulo Bluetooth HC-05;
  Display LCD-16x2;
  Potenciometro;
  Resistores;
  Objetivo: Implementar uma estação meteorologica que mostre seus dados ,obtido pelos sensores, localmente(onde está/ficará o circuito) através do display, e também, a distância.(como nesse caso optei pela transmissao do dispositivo de bluetooth.)
  modulo bluetooth hc-05
  <== Esta ligação entre j pin1 e j pin3 nao existe neste projeto!

custom parts:
  Adafruit BMP180: This precision sensor from Bosch is the best low-cost sensing solution for measuring barometric pressure and temperature. Because pressure changes with altitude you can also use it as an altimeter! The sensor is soldered onto a PCB with a 3.3V regulator, I2C level shifter and pull-up resistors on the I2C pins. The BMP180 is the next-generation of sensors from Bosch, and replaces the BMP085.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
  LCD1602-I2C: A standard character display, usually with 2x16 characters. Comes in many colors with LCM1602 IIC attached.
